// Logisim project 3-7-segment-display-book-stock.circ as structural Verilog: 1 circuit, main circuit main
module main (
);

  wire and_1_out, and_2_out, bcd_to_7_segment_1_a, bcd_to_7_segment_1_b, bcd_to_7_segment_1_c,
       bcd_to_7_segment_1_d, bcd_to_7_segment_1_e, bcd_to_7_segment_1_f, bcd_to_7_segment_1_g,
       bcd_to_7_segment_2_a, bcd_to_7_segment_2_b, bcd_to_7_segment_2_c, bcd_to_7_segment_2_d,
       bcd_to_7_segment_2_e, bcd_to_7_segment_2_f, bcd_to_7_segment_2_g, bcd_to_7_segment_3_a,
       bcd_to_7_segment_3_b, bcd_to_7_segment_3_c, bcd_to_7_segment_3_d, bcd_to_7_segment_3_e,
       bcd_to_7_segment_3_f, bcd_to_7_segment_3_g, n8bit_binary_to_bcd_1_b0, n8bit_binary_to_bcd_1_b1,
       n8bit_binary_to_bcd_1_b2, n8bit_binary_to_bcd_1_b3, n8bit_binary_to_bcd_1_b5,
       n8bit_binary_to_bcd_1_b6, n8bit_binary_to_bcd_1_b7, n8bit_binary_to_bcd_2_b4,
       n8bit_binary_to_bcd_2_b5, n8bit_binary_to_bcd_2_b6, n8bit_binary_to_bcd_2_b7, or_1_out, or_2_out,
       up_down_counter_1_a0, up_down_counter_1_a1, up_down_counter_1_a2, up_down_counter_1_a3,
       up_down_counter_2_a0, up_down_counter_2_a1, up_down_counter_2_a2, up_down_counter_2_a3, \대여_out ;

  UP_DOWN_COUNTER up_down_counter_1 (
    .down(and_1_out), .a0(up_down_counter_1_a0), .a1(up_down_counter_1_a1), .a2(up_down_counter_1_a2),
    .a3(up_down_counter_1_a3));  // open: up
  UP_DOWN_COUNTER up_down_counter_2 (
    .down(and_2_out), .a0(up_down_counter_2_a0), .a1(up_down_counter_2_a1), .a2(up_down_counter_2_a2),
    .a3(up_down_counter_2_a3));  // open: up
  _8bit_binary_to_BCD u_8bit_binary_to_bcd_1 (
    .a7(1'b0), .a6(1'b0), .a5(1'b0), .a4(1'b0), .a3(up_down_counter_1_a3), .a2(up_down_counter_1_a2),
    .a1(up_down_counter_1_a1), .a0(up_down_counter_1_a0), .b7(n8bit_binary_to_bcd_1_b7),
    .b6(n8bit_binary_to_bcd_1_b6), .b5(n8bit_binary_to_bcd_1_b5), .b4(up_down_counter_1_a1),
    .b3(n8bit_binary_to_bcd_1_b3), .b2(n8bit_binary_to_bcd_1_b2), .b1(n8bit_binary_to_bcd_1_b1),
    .b0(n8bit_binary_to_bcd_1_b0));  // open: b9, b8
  and and_1 (and_1_out, or_2_out, \대여_out );
  _8bit_binary_to_BCD u_8bit_binary_to_bcd_2 (
    .a7(1'b0), .a6(1'b0), .a5(1'b0), .a4(1'b0), .a3(up_down_counter_2_a3), .a2(up_down_counter_2_a2),
    .a1(up_down_counter_2_a1), .a0(up_down_counter_2_a0), .b7(n8bit_binary_to_bcd_2_b7),
    .b6(n8bit_binary_to_bcd_2_b6), .b5(n8bit_binary_to_bcd_2_b5), .b4(n8bit_binary_to_bcd_2_b4),
    .b3(up_down_counter_1_a1), .b2(up_down_counter_1_a1), .b1(up_down_counter_1_a1), .b0(up_down_counter_1_a1));  // open: b9, b8
  BCD_to_7_segment bcd_to_7_segment_1 (
    .On(1'b1), .A3(n8bit_binary_to_bcd_1_b3), .A2(n8bit_binary_to_bcd_1_b2), .A1(n8bit_binary_to_bcd_1_b1),
    .A0(n8bit_binary_to_bcd_1_b0), .G(bcd_to_7_segment_1_g), .F(bcd_to_7_segment_1_f),
    .E(bcd_to_7_segment_1_e), .D(bcd_to_7_segment_1_d), .C(bcd_to_7_segment_1_c), .B(bcd_to_7_segment_1_b),
    .A(bcd_to_7_segment_1_a));
  BCD_to_7_segment bcd_to_7_segment_2 (
    .On(1'b1), .A3(n8bit_binary_to_bcd_1_b7), .A2(n8bit_binary_to_bcd_1_b6), .A1(n8bit_binary_to_bcd_1_b5),
    .A0(up_down_counter_1_a1), .G(bcd_to_7_segment_2_g), .F(bcd_to_7_segment_2_f), .E(bcd_to_7_segment_2_e),
    .D(bcd_to_7_segment_2_d), .C(bcd_to_7_segment_2_c), .B(bcd_to_7_segment_2_b), .A(bcd_to_7_segment_2_a));
  BCD_to_7_segment bcd_to_7_segment_3 (
    .On(1'b1), .A3(n8bit_binary_to_bcd_2_b7), .A2(n8bit_binary_to_bcd_2_b6), .A1(n8bit_binary_to_bcd_2_b5),
    .A0(n8bit_binary_to_bcd_2_b4), .G(bcd_to_7_segment_3_g), .F(bcd_to_7_segment_3_f),
    .E(bcd_to_7_segment_3_e), .D(bcd_to_7_segment_3_d), .C(bcd_to_7_segment_3_c), .B(bcd_to_7_segment_3_b),
    .A(bcd_to_7_segment_3_a));
  or or_1 (or_1_out, up_down_counter_2_a0, up_down_counter_2_a1, up_down_counter_2_a2, up_down_counter_2_a3);
  or or_2 (or_2_out, up_down_counter_1_a0, up_down_counter_1_a1, up_down_counter_1_a2, up_down_counter_1_a3);
  Button \u_대여  (.out(\대여_out ));
  and and_2 (and_2_out, or_1_out, \대여_out );
  _7_Segment_Display u_7_segment_display_1 (
    .g(bcd_to_7_segment_2_g), .f(bcd_to_7_segment_2_f), .a(bcd_to_7_segment_2_a), .b(bcd_to_7_segment_2_b),
    .e(bcd_to_7_segment_2_e), .d(bcd_to_7_segment_2_d), .c(bcd_to_7_segment_2_c));  // open: dp
  _7_Segment_Display u_7_segment_display_2 (
    .g(bcd_to_7_segment_3_g), .f(bcd_to_7_segment_3_f), .a(bcd_to_7_segment_3_a), .b(bcd_to_7_segment_3_b),
    .e(bcd_to_7_segment_3_e), .d(bcd_to_7_segment_3_d), .c(bcd_to_7_segment_3_c));  // open: dp
  _7_Segment_Display u_7_segment_display_3 (
    .g(bcd_to_7_segment_1_g), .f(bcd_to_7_segment_1_f), .a(bcd_to_7_segment_1_a), .b(bcd_to_7_segment_1_b),
    .e(bcd_to_7_segment_1_e), .d(bcd_to_7_segment_1_d), .c(bcd_to_7_segment_1_c));  // open: dp

  // Notes on the sheet:
  //   BOOK STOCK
endmodule
