// Logisim project Digital Clock.circ as structural Verilog: 7 circuits, main circuit main
module main (
);

  wire Clock_out, colck_chip_1_a1, colck_chip_1_a2, colck_chip_1_a3, colck_chip_1_a4, colck_chip_1_a5,
       colck_chip_1_a6, colck_chip_1_b1, colck_chip_1_b2, colck_chip_1_b3, colck_chip_1_b4, colck_chip_1_b5,
       colck_chip_1_b6, colck_chip_1_c1, colck_chip_1_c2, colck_chip_1_c3, colck_chip_1_c4, colck_chip_1_c5,
       colck_chip_1_c6, colck_chip_1_d1, colck_chip_1_d2, colck_chip_1_d3, colck_chip_1_d4, colck_chip_1_d5,
       colck_chip_1_d6, colck_chip_1_e1, colck_chip_1_e2, colck_chip_1_e3, colck_chip_1_e4, colck_chip_1_e5,
       colck_chip_1_e6, colck_chip_1_f1, colck_chip_1_f2, colck_chip_1_f3, colck_chip_1_f4, colck_chip_1_f5,
       colck_chip_1_f6, colck_chip_1_g1, colck_chip_1_g2, colck_chip_1_g3, colck_chip_1_g4, colck_chip_1_g5,
       colck_chip_1_g6;

  _7_Segment_Display u_7_segment_display_1 (
    .g(colck_chip_1_g6), .f(colck_chip_1_f6), .a(colck_chip_1_a6), .b(colck_chip_1_b6), .e(colck_chip_1_e6),
    .d(colck_chip_1_d6), .c(colck_chip_1_c6));  // open: dp
  _7_Segment_Display u_7_segment_display_2 (
    .g(colck_chip_1_g5), .f(colck_chip_1_f5), .a(colck_chip_1_a5), .b(colck_chip_1_b5), .e(colck_chip_1_e5),
    .d(colck_chip_1_d5), .c(colck_chip_1_c5));  // open: dp
  _7_Segment_Display u_7_segment_display_3 (
    .g(colck_chip_1_g4), .f(colck_chip_1_f4), .a(colck_chip_1_a4), .b(colck_chip_1_b4), .e(colck_chip_1_e4),
    .d(colck_chip_1_d4), .c(colck_chip_1_c4));  // open: dp
  LED led_1 (.in(1'b1));
  LED led_2 (.in(1'b1));
  _7_Segment_Display u_7_segment_display_4 (
    .g(colck_chip_1_g3), .f(colck_chip_1_f3), .a(colck_chip_1_a3), .b(colck_chip_1_b3), .e(colck_chip_1_e3),
    .d(colck_chip_1_d3), .c(colck_chip_1_c3));  // open: dp
  LED led_3 (.in(1'b1));
  LED led_4 (.in(1'b1));
  Clock Clock (.out(Clock_out));
  _7_Segment_Display u_7_segment_display_5 (
    .g(colck_chip_1_g2), .f(colck_chip_1_f2), .a(colck_chip_1_a2), .b(colck_chip_1_b2), .e(colck_chip_1_e2),
    .d(colck_chip_1_d2), .c(colck_chip_1_c2));  // open: dp
  _7_Segment_Display u_7_segment_display_6 (
    .g(colck_chip_1_g1), .f(colck_chip_1_f1), .a(colck_chip_1_a1), .b(colck_chip_1_b1), .e(colck_chip_1_e1),
    .d(colck_chip_1_d1), .c(colck_chip_1_c1));  // open: dp
  colck_chip colck_chip_1 (
    .a6(colck_chip_1_a6), .b6(colck_chip_1_b6), .c6(colck_chip_1_c6), .d6(colck_chip_1_d6),
    .e6(colck_chip_1_e6), .f6(colck_chip_1_f6), .g6(colck_chip_1_g6), .a5(colck_chip_1_a5),
    .b5(colck_chip_1_b5), .c5(colck_chip_1_c5), .d5(colck_chip_1_d5), .e5(colck_chip_1_e5),
    .f5(colck_chip_1_f5), .g5(colck_chip_1_g5), .a4(colck_chip_1_a4), .b4(colck_chip_1_b4),
    .c4(colck_chip_1_c4), .d4(colck_chip_1_d4), .e4(colck_chip_1_e4), .f4(colck_chip_1_f4),
    .g4(colck_chip_1_g4), .a3(colck_chip_1_a3), .b3(colck_chip_1_b3), .c3(colck_chip_1_c3),
    .d3(colck_chip_1_d3), .e3(colck_chip_1_e3), .f3(colck_chip_1_f3), .g3(colck_chip_1_g3),
    .a2(colck_chip_1_a2), .b2(colck_chip_1_b2), .c2(colck_chip_1_c2), .d2(colck_chip_1_d2),
    .e2(colck_chip_1_e2), .f2(colck_chip_1_f2), .g2(colck_chip_1_g2), .a1(colck_chip_1_a1),
    .b1(colck_chip_1_b1), .c1(colck_chip_1_c1), .d1(colck_chip_1_d1), .e1(colck_chip_1_e1),
    .f1(colck_chip_1_f1), .g1(colck_chip_1_g1), .Clock(Clock_out));

  // Notes on the sheet:
  //   Digital Clock
  //   By
  //   Ali El Hadi ISMAIL FAWAZ 5460
  //   Ali AL HAKIM 5470
endmodule

module counter_div_10 (
  input  clock,
  input  pause,
  output Q4,
  output Q3,
  output Q2,
  output Q1
);

  wire and_1_out, and_2_out, and_3_out, and_4_out;

  and and_1 (and_1_out, clock, pause);
  J_K_Flip_Flop j_k_ff_1 (.J(1'b1), .clk(and_1_out), .K(1'b1), .Q(Q4), .reset(and_4_out));  // open: Qn, preset, en
  and and_2 (and_2_out, Q4, Q3);
  J_K_Flip_Flop j_k_ff_2 (.J(Q4), .clk(and_1_out), .K(Q4), .Q(Q3), .reset(and_4_out));  // open: Qn, preset, en
  J_K_Flip_Flop j_k_ff_3 (
    .J(and_2_out), .clk(and_1_out), .K(and_2_out), .Q(Q2), .reset(and_4_out));  // open: Qn, preset, en
  and and_3 (and_3_out, and_2_out, Q2);
  J_K_Flip_Flop j_k_ff_4 (
    .J(and_3_out), .clk(and_1_out), .K(and_3_out), .Q(Q1), .reset(and_4_out));  // open: Qn, preset, en
  and and_4 (and_4_out, Q1, Q3);
endmodule

module _7_segment_1digit (
  input  x1,
  input  x2,
  input  x3,
  input  x4,
  output a,
  output b,
  output c,
  output d,
  output e,
  output f,
  output g
);

  wire and_1_out, and_2_out, and_3_out, and_4_out, and_5_out, and_6_out, and_7_out, and_8_out, and_9_out,
       and_10_out, and_11_out, and_12_out, and_13_out, and_14_out, and_15_out, and_16_out, not_1_out,
       not_2_out, not_3_out, not_4_out, not_5_out, not_6_out, not_7_out, not_8_out, not_9_out, not_10_out,
       not_11_out, not_12_out, not_13_out, not_14_out, not_15_out, not_16_out, not_17_out, not_18_out,
       not_19_out, not_20_out, not_21_out;

  not not_1 (not_1_out, x2);
  and and_1 (and_1_out, not_1_out, not_2_out);
  not not_2 (not_2_out, x4);
  and and_2 (and_2_out, x2, x4);
  not not_3 (not_3_out, x2);
  not not_4 (not_4_out, x3);
  and and_3 (and_3_out, not_4_out, not_5_out);
  not not_5 (not_5_out, x4);
  and and_4 (and_4_out, x3, x4);
  not not_6 (not_6_out, x3);
  or or_1 (c, not_6_out, x4, x2);
  not not_7 (not_7_out, x2);
  and and_5 (and_5_out, not_7_out, not_8_out);
  not not_8 (not_8_out, x4);
  not not_9 (not_9_out, x2);
  and and_6 (and_6_out, not_9_out, x3);
  and and_7 (and_7_out, x3, not_10_out);
  not not_10 (not_10_out, x4);
  and and_8 (and_8_out, x2, not_11_out, x4);
  not not_11 (not_11_out, x3);
  not not_12 (not_12_out, x2);
  and and_9 (and_9_out, not_12_out, not_13_out);
  not not_13 (not_13_out, x4);
  and and_10 (and_10_out, x3, not_14_out);
  not not_14 (not_14_out, x4);
  not not_15 (not_15_out, x3);
  and and_11 (and_11_out, not_15_out, not_16_out);
  not not_16 (not_16_out, x4);
  and and_12 (and_12_out, x2, not_17_out);
  not not_17 (not_17_out, x3);
  and and_13 (and_13_out, x2, not_18_out);
  not not_18 (not_18_out, x4);
  not not_19 (not_19_out, x2);
  and and_14 (and_14_out, not_19_out, x3);
  and and_15 (and_15_out, x2, not_20_out);
  not not_20 (not_20_out, x3);
  and and_16 (and_16_out, x2, not_21_out);
  not not_21 (not_21_out, x4);
  or or_2 (a, and_1_out, x3, and_2_out, x1);
  or or_3 (b, not_3_out, and_3_out, and_4_out);
  or or_4 (d, and_5_out, and_6_out, and_7_out, and_8_out, x1);
  or or_5 (e, and_9_out, and_10_out);
  or or_6 (f, and_11_out, and_12_out, and_13_out, x1);
  or or_7 (g, and_14_out, and_15_out, and_16_out, x1);
endmodule

module counter_div_6 (
  input  clock,
  input  pause,
  output Q4,
  output Q3,
  output Q2,
  output Q1
);

  wire and_1_out, and_2_out, and_3_out, and_4_out;

  and and_1 (and_1_out, clock, pause);
  J_K_Flip_Flop j_k_ff_1 (.J(1'b1), .clk(and_1_out), .K(1'b1), .Q(Q4), .reset(and_4_out));  // open: Qn, preset, en
  and and_2 (and_2_out, Q4, Q3);
  J_K_Flip_Flop j_k_ff_2 (.J(Q4), .clk(and_1_out), .K(Q4), .Q(Q3), .reset(and_4_out));  // open: Qn, preset, en
  J_K_Flip_Flop j_k_ff_3 (
    .J(and_2_out), .clk(and_1_out), .K(and_2_out), .Q(Q2), .reset(and_4_out));  // open: Qn, preset, en
  and and_3 (and_3_out, and_2_out, Q2);
  J_K_Flip_Flop j_k_ff_4 (
    .J(and_3_out), .clk(and_1_out), .K(and_3_out), .Q(Q1), .reset(and_4_out));  // open: Qn, preset, en
  and and_4 (and_4_out, Q2, Q3);
endmodule

module colck_chip (
  input  Clock,
  output a6,
  output b6,
  output c6,
  output d6,
  output e6,
  output f6,
  output g6,
  output a5,
  output b5,
  output c5,
  output d5,
  output e5,
  output f5,
  output g5,
  output a4,
  output b4,
  output c4,
  output d4,
  output e4,
  output f4,
  output g4,
  output a3,
  output b3,
  output c3,
  output d3,
  output e3,
  output f3,
  output g3,
  output a2,
  output b2,
  output c2,
  output d2,
  output e2,
  output f2,
  output g2,
  output a1,
  output b1,
  output c1,
  output d1,
  output e1,
  output f1,
  output g1
);

  wire and_1_out, and_2_out, and_3_out, and_4_out, and_5_out, and_6_out, counter_div_2_1_q1,
       counter_div_2_1_q2, counter_div_6_1_q1, counter_div_6_1_q2, counter_div_6_1_q3, counter_div_6_1_q4,
       counter_div_6_2_q1, counter_div_6_2_q2, counter_div_6_2_q3, counter_div_6_2_q4, counter_div_10_1_q1,
       counter_div_10_1_q2, counter_div_10_1_q3, counter_div_10_1_q4, counter_div_10_2_q1,
       counter_div_10_2_q2, counter_div_10_2_q3, counter_div_10_2_q4, counter_div_input_1_q1,
       counter_div_input_1_q2, counter_div_input_1_q3, counter_div_input_1_q4, or_1_out;

  _7_segment_1digit u_7_segment_1digit_1 (
    .x1(1'b0), .x2(1'b0), .x3(counter_div_2_1_q1), .x4(counter_div_2_1_q2), .a(a6), .b(b6), .c(c6), .d(d6),
    .e(e6), .f(f6), .g(g6));
  or or_1 (or_1_out, and_2_out, and_1_out);
  counter_div_2 counter_div_2_1 (.Clock(Clock), .Pause(or_1_out), .Q2(counter_div_2_1_q2), .Q1(counter_div_2_1_q1));
  and and_1 (and_1_out, counter_div_input_1_q1, counter_div_input_1_q3);
  _7_segment_1digit u_7_segment_1digit_2 (
    .x1(counter_div_input_1_q1), .x2(counter_div_input_1_q2), .x3(counter_div_input_1_q3),
    .x4(counter_div_input_1_q4), .a(a5), .b(b5), .c(c5), .d(d5), .e(e5), .f(f5), .g(g5));
  counter_div_input counter_div_input_1 (
    .clock(Clock), .pause(and_3_out), .Q4(counter_div_input_1_q4), .Q3(counter_div_input_1_q3),
    .Q2(counter_div_input_1_q2), .Q1(counter_div_input_1_q1), .reset_hour_2(and_2_out));
  and and_2 (and_2_out, counter_div_2_1_q1, counter_div_input_1_q2);
  and and_3 (and_3_out, counter_div_6_1_q2, counter_div_6_1_q3);
  _7_segment_1digit u_7_segment_1digit_3 (
    .x1(counter_div_6_1_q1), .x2(counter_div_6_1_q2), .x3(counter_div_6_1_q3), .x4(counter_div_6_1_q4),
    .a(a4), .b(b4), .c(c4), .d(d4), .e(e4), .f(f4), .g(g4));
  counter_div_6 counter_div_6_1 (
    .clock(Clock), .pause(and_4_out), .Q4(counter_div_6_1_q4), .Q3(counter_div_6_1_q3),
    .Q2(counter_div_6_1_q2), .Q1(counter_div_6_1_q1));
  and and_4 (and_4_out, counter_div_10_1_q1, counter_div_10_1_q3);
  _7_segment_1digit u_7_segment_1digit_4 (
    .x1(counter_div_10_1_q1), .x2(counter_div_10_1_q2), .x3(counter_div_10_1_q3), .x4(counter_div_10_1_q4),
    .a(a3), .b(b3), .c(c3), .d(d3), .e(e3), .f(f3), .g(g3));
  counter_div_10 counter_div_10_1 (
    .clock(Clock), .pause(and_5_out), .Q4(counter_div_10_1_q4), .Q3(counter_div_10_1_q3),
    .Q2(counter_div_10_1_q2), .Q1(counter_div_10_1_q1));
  and and_5 (and_5_out, counter_div_6_2_q2, counter_div_6_2_q3);
  _7_segment_1digit u_7_segment_1digit_5 (
    .x1(counter_div_6_2_q1), .x2(counter_div_6_2_q2), .x3(counter_div_6_2_q3), .x4(counter_div_6_2_q4),
    .a(a2), .b(b2), .c(c2), .d(d2), .e(e2), .f(f2), .g(g2));
  counter_div_6 counter_div_6_2 (
    .clock(Clock), .pause(and_6_out), .Q4(counter_div_6_2_q4), .Q3(counter_div_6_2_q3),
    .Q2(counter_div_6_2_q2), .Q1(counter_div_6_2_q1));
  and and_6 (and_6_out, counter_div_10_2_q3, counter_div_10_2_q1);
  _7_segment_1digit u_7_segment_1digit_6 (
    .x1(counter_div_10_2_q1), .x2(counter_div_10_2_q2), .x3(counter_div_10_2_q3), .x4(counter_div_10_2_q4),
    .a(a1), .b(b1), .c(c1), .d(d1), .e(e1), .f(f1), .g(g1));
  counter_div_10 counter_div_10_2 (
    .clock(Clock), .pause(1'b1), .Q4(counter_div_10_2_q4), .Q3(counter_div_10_2_q3),
    .Q2(counter_div_10_2_q2), .Q1(counter_div_10_2_q1));
endmodule

module counter_div_2 (
  input  Clock,
  input  Pause,
  output Q2,
  output Q1
);

  wire and_1_out, and_2_out;

  and and_1 (and_1_out, Clock, Pause);
  J_K_Flip_Flop j_k_ff_1 (.J(1'b1), .clk(and_1_out), .K(1'b1), .Q(Q2), .reset(and_2_out));  // open: Qn, preset, en
  J_K_Flip_Flop j_k_ff_2 (.J(Q2), .clk(and_1_out), .K(Q2), .Q(Q1), .reset(and_2_out));  // open: Qn, preset, en
  and and_2 (and_2_out, Q2, Q1);
endmodule

module counter_div_input (
  input  clock,
  input  reset_hour_2,
  input  pause,
  output Q4,
  output Q3,
  output Q2,
  output Q1
);

  wire and_1_out, and_2_out, and_3_out, and_4_out, or_1_out;

  J_K_Flip_Flop j_k_ff_1 (.J(1'b1), .clk(and_1_out), .K(1'b1), .Q(Q4), .reset(or_1_out));  // open: Qn, preset, en
  and and_1 (and_1_out, clock, pause);
  J_K_Flip_Flop j_k_ff_2 (.J(Q4), .clk(and_1_out), .K(Q4), .Q(Q3), .reset(or_1_out));  // open: Qn, preset, en
  and and_2 (and_2_out, Q4, Q3);
  and and_3 (and_3_out, and_2_out, Q2);
  J_K_Flip_Flop j_k_ff_3 (
    .J(and_2_out), .clk(and_1_out), .K(and_2_out), .Q(Q2), .reset(or_1_out));  // open: Qn, preset, en
  J_K_Flip_Flop j_k_ff_4 (
    .J(and_3_out), .clk(and_1_out), .K(and_3_out), .Q(Q1), .reset(or_1_out));  // open: Qn, preset, en
  or or_1 (or_1_out, and_4_out, reset_hour_2);
  and and_4 (and_4_out, Q3, Q1);
endmodule
