// Logisim project bookreturn(Final).circ as structural Verilog: 9 circuits, main circuit main
module main (
  input  book_loans,
  input  in_2,
  input  in_3,
  input  in_4,
  input  in_5,
  input  in_6,
  input  in_7,
  output out_8,
  output out_9,
  output out_10,
  output out_11,
  output [3:0] out_12,
  output [3:0] out_13
);

  wire and_1_out, and_2_out, bcd_to_7_segment_1_a, bcd_to_7_segment_1_b, bcd_to_7_segment_1_c,
       bcd_to_7_segment_1_d, bcd_to_7_segment_1_e, bcd_to_7_segment_1_f, bcd_to_7_segment_1_g,
       bcd_to_7_segment_2_a, bcd_to_7_segment_2_b, bcd_to_7_segment_2_c, bcd_to_7_segment_2_d,
       bcd_to_7_segment_2_e, bcd_to_7_segment_2_f, bcd_to_7_segment_2_g, bcd_to_7_segment_3_a,
       bcd_to_7_segment_3_b, bcd_to_7_segment_3_c, bcd_to_7_segment_3_d, bcd_to_7_segment_3_e,
       bcd_to_7_segment_3_f, bcd_to_7_segment_3_g, button_1_out, clock_1_out, comparator_1_eq,
       comparator_1_gt, comparator_1_lt, j_k_ff_2_qn, j_k_ff_3_qn, j_k_ff_4_qn, j_k_ff_5_q,
       n7_segment_display_driver_1_p5, n7_segment_display_driver_1_p6, n7_segment_display_driver_1_p7,
       n7_segment_display_driver_1_p8, n7_segment_display_driver_1_p9, n7_segment_display_driver_1_p10,
       n7_segment_display_driver_1_p11, n7_segment_display_driver_2_p5, n7_segment_display_driver_2_p6,
       n7_segment_display_driver_2_p7, n7_segment_display_driver_2_p8, n7_segment_display_driver_2_p9,
       n7_segment_display_driver_2_p10, n7_segment_display_driver_2_p11, n8bit_binary_to_bcd_1_b0,
       n8bit_binary_to_bcd_1_b1, n8bit_binary_to_bcd_1_b2, n8bit_binary_to_bcd_1_b3,
       n8bit_binary_to_bcd_1_b4, n8bit_binary_to_bcd_1_b5, n8bit_binary_to_bcd_1_b6,
       n8bit_binary_to_bcd_1_b7, n8bit_binary_to_bcd_2_b0, n8bit_binary_to_bcd_2_b1,
       n8bit_binary_to_bcd_2_b2, n8bit_binary_to_bcd_2_b3, n8bit_binary_to_bcd_2_b4,
       n8bit_binary_to_bcd_2_b5, n8bit_binary_to_bcd_2_b6, n8bit_binary_to_bcd_2_b7, not_1_out, or_1_out,
       or_2_out, up_down_counter_1_a0, up_down_counter_1_a1, up_down_counter_1_a2, up_down_counter_1_a3,
       up_down_counter_2_a0, up_down_counter_2_a1, up_down_counter_2_a2, up_down_counter_2_a3;

  Button button_1 (.out(button_1_out));
  UP_DOWN_COUNTER up_down_counter_1 (
    .up(button_1_out), .down(and_1_out), .a0(up_down_counter_1_a0), .a1(up_down_counter_1_a1),
    .a2(up_down_counter_1_a2), .a3(up_down_counter_1_a3));
  UP_DOWN_COUNTER up_down_counter_2 (
    .up(button_1_out), .down(and_2_out), .a0(up_down_counter_2_a0), .a1(up_down_counter_2_a1),
    .a2(up_down_counter_2_a2), .a3(up_down_counter_2_a3));
  _8bit_binary_to_BCD u_8bit_binary_to_bcd_1 (
    .a7(1'b0), .a6(1'b0), .a5(1'b0), .a4(1'b0), .a3(up_down_counter_1_a3), .a2(up_down_counter_1_a2),
    .a1(up_down_counter_1_a1), .a0(up_down_counter_1_a0), .b7(n8bit_binary_to_bcd_1_b7),
    .b6(n8bit_binary_to_bcd_1_b6), .b5(n8bit_binary_to_bcd_1_b5), .b4(n8bit_binary_to_bcd_1_b4),
    .b3(n8bit_binary_to_bcd_1_b3), .b2(n8bit_binary_to_bcd_1_b2), .b1(n8bit_binary_to_bcd_1_b1),
    .b0(n8bit_binary_to_bcd_1_b0));  // open: b9, b8
  _8bit_binary_to_BCD u_8bit_binary_to_bcd_2 (
    .a7(1'b0), .a6(1'b0), .a5(1'b0), .a4(1'b0), .a3(up_down_counter_2_a3), .a2(up_down_counter_2_a2),
    .a1(up_down_counter_2_a1), .a0(up_down_counter_2_a0), .b7(n8bit_binary_to_bcd_2_b7),
    .b6(n8bit_binary_to_bcd_2_b6), .b5(n8bit_binary_to_bcd_2_b5), .b4(n8bit_binary_to_bcd_2_b4),
    .b3(n8bit_binary_to_bcd_2_b3), .b2(n8bit_binary_to_bcd_2_b2), .b1(n8bit_binary_to_bcd_2_b1),
    .b0(n8bit_binary_to_bcd_2_b0));  // open: b9, b8
  and and_1 (and_1_out, or_2_out, book_loans);
  or or_1 (or_1_out, up_down_counter_2_a0, up_down_counter_2_a1, up_down_counter_2_a2, up_down_counter_2_a3);
  BCD_to_7_segment bcd_to_7_segment_1 (
    .On(1'b1), .A3(n8bit_binary_to_bcd_1_b3), .A2(n8bit_binary_to_bcd_1_b2), .A1(n8bit_binary_to_bcd_1_b1),
    .A0(n8bit_binary_to_bcd_1_b0), .G(bcd_to_7_segment_1_g), .F(bcd_to_7_segment_1_f),
    .E(bcd_to_7_segment_1_e), .D(bcd_to_7_segment_1_d), .C(bcd_to_7_segment_1_c), .B(bcd_to_7_segment_1_b),
    .A(bcd_to_7_segment_1_a));
  BCD_to_7_segment bcd_to_7_segment_2 (
    .On(1'b1), .A3(n8bit_binary_to_bcd_1_b7), .A2(n8bit_binary_to_bcd_1_b6), .A1(n8bit_binary_to_bcd_1_b5),
    .A0(n8bit_binary_to_bcd_1_b4), .G(bcd_to_7_segment_2_g), .F(bcd_to_7_segment_2_f),
    .E(bcd_to_7_segment_2_e), .D(bcd_to_7_segment_2_d), .C(bcd_to_7_segment_2_c), .B(bcd_to_7_segment_2_b),
    .A(bcd_to_7_segment_2_a));
  BCD_to_7_segment bcd_to_7_segment_3 (
    .On(1'b1), .A3(n8bit_binary_to_bcd_2_b7), .A2(n8bit_binary_to_bcd_2_b6), .A1(n8bit_binary_to_bcd_2_b5),
    .A0(n8bit_binary_to_bcd_2_b4), .G(bcd_to_7_segment_3_g), .F(bcd_to_7_segment_3_f),
    .E(bcd_to_7_segment_3_e), .D(bcd_to_7_segment_3_d), .C(bcd_to_7_segment_3_c), .B(bcd_to_7_segment_3_b),
    .A(bcd_to_7_segment_3_a));
  or or_2 (or_2_out, up_down_counter_1_a0, n8bit_binary_to_bcd_2_b0, up_down_counter_1_a2, up_down_counter_1_a3);
  and and_2 (and_2_out, or_1_out, book_loans);
  _7_Segment_Display u_7_segment_display_1 (
    .g(bcd_to_7_segment_3_g), .f(bcd_to_7_segment_3_f), .a(bcd_to_7_segment_3_a), .b(bcd_to_7_segment_3_b),
    .e(bcd_to_7_segment_3_e), .d(bcd_to_7_segment_3_d), .c(bcd_to_7_segment_3_c));  // open: dp
  _7_Segment_Display u_7_segment_display_2 (
    .g(bcd_to_7_segment_1_g), .f(bcd_to_7_segment_1_f), .a(bcd_to_7_segment_1_a), .b(bcd_to_7_segment_1_b),
    .e(bcd_to_7_segment_1_e), .d(bcd_to_7_segment_1_d), .c(bcd_to_7_segment_1_c));  // open: dp
  _7_Segment_Display u_7_segment_display_3 (
    .g(bcd_to_7_segment_2_g), .f(bcd_to_7_segment_2_f), .a(bcd_to_7_segment_2_a), .b(bcd_to_7_segment_2_b),
    .e(bcd_to_7_segment_2_e), .d(bcd_to_7_segment_2_d), .c(bcd_to_7_segment_2_c));  // open: dp
  not not_1 (not_1_out, book_loans);
  Clock clock_1 (.out(clock_1_out));
  J_K_Flip_Flop j_k_ff_1 (.J(not_1_out), .clk(j_k_ff_2_qn), .K(not_1_out), .Q(out_8));  // open: Qn, preset, en, reset
  J_K_Flip_Flop j_k_ff_2 (
    .J(not_1_out), .clk(j_k_ff_3_qn), .K(not_1_out), .Q(out_9), .Qn(j_k_ff_2_qn));  // open: preset, en, reset
  J_K_Flip_Flop j_k_ff_3 (
    .J(not_1_out), .clk(j_k_ff_4_qn), .K(not_1_out), .Q(out_10), .Qn(j_k_ff_3_qn));  // open: preset, en, reset
  J_K_Flip_Flop j_k_ff_4 (
    .J(not_1_out), .clk(clock_1_out), .K(not_1_out), .Q(out_11), .Qn(j_k_ff_4_qn));  // open: preset, en, reset
  // _7_segment_display_driver 7_segment_display_driver_1: pin names not known; wires that end beside it: out_8, out_9, out_10, out_11, n7_segment_display_driver_1_p5, n7_segment_display_driver_1_p6, n7_segment_display_driver_1_p7, n7_segment_display_driver_1_p8, n7_segment_display_driver_1_p9, n7_segment_display_driver_1_p10, n7_segment_display_driver_1_p11
  // _7_segment_display_driver 7_segment_display_driver_2: pin names not known; wires that end beside it: in_2, in_3, in_4, in_5, n7_segment_display_driver_2_p5, n7_segment_display_driver_2_p6, n7_segment_display_driver_2_p7, n7_segment_display_driver_2_p8, n7_segment_display_driver_2_p9, n7_segment_display_driver_2_p10, n7_segment_display_driver_2_p11
  _7_Segment_Display u_7_segment_display_4 (
    .g(n7_segment_display_driver_1_p11), .f(n7_segment_display_driver_1_p10),
    .a(n7_segment_display_driver_1_p5), .b(n7_segment_display_driver_1_p6),
    .e(n7_segment_display_driver_1_p9), .d(n7_segment_display_driver_1_p8), .c(n7_segment_display_driver_1_p7));  // open: dp
  _7_Segment_Display u_7_segment_display_5 (
    .g(n7_segment_display_driver_2_p11), .f(n7_segment_display_driver_2_p10),
    .a(n7_segment_display_driver_2_p5), .b(n7_segment_display_driver_2_p6),
    .e(n7_segment_display_driver_2_p9), .d(n7_segment_display_driver_2_p8), .c(n7_segment_display_driver_2_p7));  // open: dp
  J_K_Flip_Flop j_k_ff_5 (.J(in_6), .clk(comparator_1_eq), .K(in_7), .Q(j_k_ff_5_q));  // open: Qn, preset, en, reset
  LED led_1 (.in(comparator_1_gt));
  Comparator #(.width(4)) comparator_1 (
    .a({out_8, out_9, out_10, out_11}), .b({in_2, in_3, in_4, in_5}), .gt(comparator_1_gt),
    .eq(comparator_1_eq), .lt(comparator_1_lt));
  LED led_2 (.in(comparator_1_lt));
  _7_Segment_Display u_7_segment_display_6 (.b(j_k_ff_5_q), .c(j_k_ff_5_q));  // open: g, f, a, e, d, dp
  _7_Segment_Display u_7_segment_display_7 (
    .f(j_k_ff_5_q), .a(j_k_ff_5_q), .b(j_k_ff_5_q), .e(j_k_ff_5_q), .d(j_k_ff_5_q), .c(j_k_ff_5_q));  // open: g, dp
  _7_Segment_Display u_7_segment_display_8 (
    .f(j_k_ff_5_q), .a(j_k_ff_5_q), .b(j_k_ff_5_q), .e(j_k_ff_5_q), .d(j_k_ff_5_q), .c(j_k_ff_5_q));  // open: g, dp
  _7_Segment_Display u_7_segment_display_9 (
    .f(j_k_ff_5_q), .a(j_k_ff_5_q), .b(j_k_ff_5_q), .e(j_k_ff_5_q), .d(j_k_ff_5_q), .c(j_k_ff_5_q));  // open: g, dp

  assign out_12 = {out_8, out_9, out_10, out_11};
  assign out_13 = {in_2, in_3, in_4, in_5};

  // Notes on the sheet:
  //   book return
endmodule

module add3 (
  input  A3,
  input  A2,
  input  A1,
  input  A0,
  output S3,
  output S2,
  output S1,
  output S0
);

  wire and_1_out, and_2_out, and_3_out, and_4_out, and_5_out, and_6_out, and_7_out, and_8_out, and_9_out,
       and_10_out, and_11_out, and_12_out, and_13_out, and_14_out, not_1_out, not_2_out, not_3_out,
       not_4_out, not_5_out, not_6_out, not_7_out, not_8_out, not_9_out, not_10_out, not_11_out, not_12_out,
       not_13_out, not_14_out, not_15_out, not_16_out;

  and and_1 (and_1_out, A2, A0);
  and and_2 (and_2_out, A2, A1);
  not not_1 (not_1_out, A1);
  and and_3 (and_3_out, A2, not_1_out, not_2_out);
  not not_2 (not_2_out, A0);
  and and_4 (and_4_out, A3, not_3_out, A0);
  not not_3 (not_3_out, A1);
  and and_5 (and_5_out, A3, A1, not_4_out);
  not not_4 (not_4_out, A0);
  and and_6 (and_6_out, A3, A2);
  not not_5 (not_5_out, A3);
  not not_6 (not_6_out, A2);
  and and_7 (and_7_out, not_5_out, not_6_out, A1);
  not not_7 (not_7_out, A3);
  and and_8 (and_8_out, not_7_out, A1, A0);
  not not_8 (not_8_out, A2);
  and and_9 (and_9_out, A3, not_8_out, not_9_out);
  not not_9 (not_9_out, A0);
  and and_10 (and_10_out, A3, A2, not_10_out);
  not not_10 (not_10_out, A1);
  not not_11 (not_11_out, A3);
  not not_12 (not_12_out, A2);
  not not_13 (not_13_out, A0);
  not not_14 (not_14_out, A2);
  not not_15 (not_15_out, A0);
  not not_16 (not_16_out, A1);
  or or_1 (S3, and_1_out, and_2_out, A3);
  or or_2 (S2, and_3_out, and_4_out, and_5_out, and_6_out);
  or or_3 (S1, and_7_out, and_8_out, and_9_out, and_10_out);
  and and_11 (and_11_out, not_11_out, not_12_out, A0);
  and and_12 (and_12_out, A2, A1, not_13_out);
  and and_13 (and_13_out, A3, not_14_out, not_15_out);
  and and_14 (and_14_out, A3, A2, not_16_out, A0);
  or or_4 (S0, and_11_out, and_12_out, and_13_out, and_14_out);
endmodule

module _8bit_binary_to_BCD (
  input  a7,
  input  a6,
  input  a5,
  input  a4,
  input  a3,
  input  a2,
  input  a1,
  input  a0,
  output b9,
  output b8,
  output b7,
  output b6,
  output b5,
  output b4,
  output b3,
  output b2,
  output b1,
  output b0
);

  wire add3_1_s0, add3_1_s1, add3_1_s2, add3_1_s3, add3_2_s0, add3_2_s1, add3_2_s2, add3_2_s3, add3_3_s0,
       add3_3_s1, add3_3_s2, add3_5_s0, add3_5_s1, add3_5_s2, add3_5_s3, add3_6_s0, add3_6_s1, add3_6_s2,
       add3_6_s3;

  add3 add3_1 (.A3(1'b0), .A2(a7), .S3(add3_1_s3), .A1(a6), .A0(a5), .S2(add3_1_s2), .S1(add3_1_s1), .S0(add3_1_s0));
  add3 add3_2 (
    .A3(add3_1_s2), .A2(add3_1_s1), .S3(add3_2_s3), .A1(add3_1_s0), .A0(a4), .S2(add3_2_s2), .S1(add3_2_s1),
    .S0(add3_2_s0));
  add3 add3_3 (
    .A3(1'b0), .A2(add3_1_s3), .S3(b9), .A1(add3_2_s3), .A0(add3_5_s3), .S2(add3_3_s2), .S1(add3_3_s1),
    .S0(add3_3_s0));
  add3 add3_4 (.A3(add3_3_s2), .A2(add3_3_s1), .S3(b8), .A1(add3_3_s0), .A0(add3_6_s3), .S2(b7), .S1(b6), .S0(b5));
  add3 add3_5 (
    .A3(add3_2_s2), .A2(add3_2_s1), .S3(add3_5_s3), .A1(add3_2_s0), .A0(a3), .S2(add3_5_s2), .S1(add3_5_s1),
    .S0(add3_5_s0));
  add3 add3_6 (
    .A3(add3_5_s2), .A2(add3_5_s1), .S3(add3_6_s3), .A1(add3_5_s0), .A0(a2), .S2(add3_6_s2), .S1(add3_6_s1),
    .S0(add3_6_s0));
  add3 add3_7 (.A3(add3_6_s2), .A2(add3_6_s1), .S3(b4), .A1(add3_6_s0), .A0(a1), .S2(b3), .S1(b2), .S0(b1));

  assign b0 = a0;
endmodule

module BCD_to_7_segment (
  input  On,
  input  A3,
  input  A2,
  input  A1,
  input  A0,
  output G,
  output F,
  output E,
  output D,
  output C,
  output B,
  output A
);

  wire not_1_out, not_2_out, not_3_out, not_4_out, not_5_out, not_6_out, not_7_out, not_8_out, not_9_out,
       not_10_out, not_11_out, not_12_out, not_13_out, not_14_out, not_15_out, not_16_out, not_17_out,
       not_18_out, not_19_out, not_20_out, not_21_out, or_1_out, or_2_out, or_3_out, or_4_out, or_5_out,
       or_6_out, or_7_out, or_8_out, or_9_out, or_10_out, or_11_out, or_12_out, or_13_out, or_14_out;

  not not_1 (not_1_out, A2);
  not not_2 (not_2_out, A1);
  not not_3 (not_3_out, A0);
  not not_4 (not_4_out, A0);
  not not_5 (not_5_out, A1);
  not not_6 (not_6_out, A1);
  not not_7 (not_7_out, A0);
  not not_8 (not_8_out, A2);
  not not_9 (not_9_out, A0);
  not not_10 (not_10_out, A2);
  not not_11 (not_11_out, A2);
  not not_12 (not_12_out, A1);
  not not_13 (not_13_out, A0);
  not not_14 (not_14_out, A1);
  not not_15 (not_15_out, A2);
  not not_16 (not_16_out, A0);
  not not_17 (not_17_out, A2);
  not not_18 (not_18_out, A1);
  not not_19 (not_19_out, A0);
  not not_20 (not_20_out, A2);
  or or_1 (or_1_out, A3, A2, A1);
  or or_2 (or_2_out, not_1_out, not_2_out, not_3_out);
  or or_3 (or_3_out, A3, A2, not_4_out);
  or or_4 (or_4_out, A2, not_5_out);
  or or_5 (or_5_out, not_6_out, not_7_out);
  not not_21 (not_21_out, A0);
  or or_6 (or_6_out, not_8_out, A1);
  or or_7 (or_7_out, A3, A2, A1, not_9_out);
  or or_8 (or_8_out, not_10_out, A1, A0);
  or or_9 (or_9_out, not_11_out, not_12_out, not_13_out);
  or or_10 (or_10_out, A2, not_14_out, A0);
  or or_11 (or_11_out, not_15_out, A1, not_16_out);
  or or_12 (or_12_out, not_17_out, not_18_out, A0);
  or or_13 (or_13_out, A3, A2, A1, not_19_out);
  or or_14 (or_14_out, not_20_out, A1, A0);
  and and_1 (G, On, or_1_out, or_2_out);
  and and_2 (F, On, or_3_out, or_4_out, or_5_out);
  and and_3 (E, On, not_21_out, or_6_out);
  and and_4 (D, On, or_7_out, or_8_out, or_9_out);
  and and_5 (C, On, or_10_out);
  and and_6 (B, On, or_11_out, or_12_out);
  and and_7 (A, On, or_13_out, or_14_out);
endmodule

module day_count (
  output A0,
  output A1,
  output A2,
  output A3,
  output A4,
  output A5,
  output A6,
  output A7,
  output A8,
  output A9,
  output A10,
  output A11,
  output A12,
  output A13,
  output A14,
  output A15
);

  wire and_1_out, and_2_out, and_3_out, and_4_out, and_5_out, and_6_out, and_7_out, and_8_out, and_9_out,
       and_10_out, and_11_out, and_12_out, and_13_out, and_14_out, clock_1_out;

  Clock clock_1 (.out(clock_1_out));
  J_K_Flip_Flop j_k_ff_1 (.J(1'b1), .clk(clock_1_out), .K(1'b1), .Q(A0));  // open: Qn, preset, en, reset
  and and_1 (and_1_out, A0, A1);
  J_K_Flip_Flop j_k_ff_2 (.J(A0), .clk(clock_1_out), .K(A0), .Q(A1));  // open: Qn, preset, en, reset
  and and_2 (and_2_out, and_13_out, A8);
  J_K_Flip_Flop j_k_ff_3 (.J(and_13_out), .clk(clock_1_out), .K(and_13_out), .Q(A8));  // open: Qn, preset, en, reset
  J_K_Flip_Flop j_k_ff_4 (.J(and_1_out), .clk(clock_1_out), .K(and_1_out), .Q(A2));  // open: Qn, preset, en, reset
  J_K_Flip_Flop j_k_ff_5 (.J(and_2_out), .clk(clock_1_out), .K(and_2_out), .Q(A9));  // open: Qn, preset, en, reset
  and and_3 (and_3_out, and_1_out, A2);
  and and_4 (and_4_out, and_2_out, A9);
  J_K_Flip_Flop j_k_ff_6 (.J(and_3_out), .clk(clock_1_out), .K(and_3_out), .Q(A3));  // open: Qn, preset, en, reset
  J_K_Flip_Flop j_k_ff_7 (.J(and_4_out), .clk(clock_1_out), .K(and_4_out), .Q(A10));  // open: Qn, preset, en, reset
  and and_5 (and_5_out, and_3_out, A3);
  and and_6 (and_6_out, and_4_out, A10);
  and and_7 (and_7_out, and_5_out, A4);
  J_K_Flip_Flop j_k_ff_8 (.J(and_5_out), .clk(clock_1_out), .K(and_5_out), .Q(A4));  // open: Qn, preset, en, reset
  and and_8 (and_8_out, and_6_out, A11);
  J_K_Flip_Flop j_k_ff_9 (.J(and_6_out), .clk(clock_1_out), .K(and_6_out), .Q(A11));  // open: Qn, preset, en, reset
  J_K_Flip_Flop j_k_ff_10 (.J(and_7_out), .clk(clock_1_out), .K(and_7_out), .Q(A5));  // open: Qn, preset, en, reset
  J_K_Flip_Flop j_k_ff_11 (.J(and_8_out), .clk(clock_1_out), .K(and_8_out), .Q(A12));  // open: Qn, preset, en, reset
  and and_9 (and_9_out, and_7_out, A5);
  and and_10 (and_10_out, and_8_out, A12);
  J_K_Flip_Flop j_k_ff_12 (.J(and_9_out), .clk(clock_1_out), .K(and_9_out), .Q(A6));  // open: Qn, preset, en, reset
  J_K_Flip_Flop j_k_ff_13 (.J(and_10_out), .clk(clock_1_out), .K(and_10_out), .Q(A13));  // open: Qn, preset, en, reset
  and and_11 (and_11_out, and_9_out, A6);
  and and_12 (and_12_out, and_10_out, A13);
  and and_13 (and_13_out, and_11_out, A7);
  J_K_Flip_Flop j_k_ff_14 (.J(and_11_out), .clk(clock_1_out), .K(and_11_out), .Q(A7));  // open: Qn, preset, en, reset
  and and_14 (and_14_out, and_12_out, A14);
  J_K_Flip_Flop j_k_ff_15 (.J(and_12_out), .clk(clock_1_out), .K(and_12_out), .Q(A14));  // open: Qn, preset, en, reset
  J_K_Flip_Flop j_k_ff_16 (.J(and_14_out), .clk(clock_1_out), .K(and_14_out), .Q(A15));  // open: Qn, preset, en, reset
endmodule

module _5_bit_jk_up_counter (
  input  in_1,
  output a0,
  output a1,
  output a2,
  output a3,
  output a4
);

  wire j_k_ff_1_qn, j_k_ff_2_qn, j_k_ff_3_qn, j_k_ff_4_qn;

  J_K_Flip_Flop j_k_ff_1 (.J(1'b1), .clk(in_1), .K(1'b1), .Q(a0), .Qn(j_k_ff_1_qn));  // open: preset, en, reset
  J_K_Flip_Flop j_k_ff_2 (.J(1'b1), .clk(j_k_ff_1_qn), .K(1'b1), .Q(a1), .Qn(j_k_ff_2_qn));  // open: preset, en, reset
  J_K_Flip_Flop j_k_ff_3 (.J(1'b1), .clk(j_k_ff_2_qn), .K(1'b1), .Q(a2), .Qn(j_k_ff_3_qn));  // open: preset, en, reset
  J_K_Flip_Flop j_k_ff_4 (.J(1'b1), .clk(j_k_ff_3_qn), .K(1'b1), .Q(a3), .Qn(j_k_ff_4_qn));  // open: preset, en, reset
  J_K_Flip_Flop j_k_ff_5 (.J(1'b1), .clk(j_k_ff_4_qn), .K(1'b1), .Q(a4));  // open: Qn, preset, en, reset
endmodule

module _16_bit_subtractor (
  input  b16,
  input  b15,
  input  b14,
  input  b13,
  input  a16,
  input  a15,
  input  a14,
  input  a13,
  input  b12,
  input  b11,
  input  b10,
  input  b9,
  input  a12,
  input  a11,
  input  a10,
  input  a9,
  input  b8,
  input  b7,
  input  b6,
  input  b5,
  input  a8,
  input  a7,
  input  a6,
  input  a5,
  input  b4,
  input  b3,
  input  b2,
  input  b1,
  input  a4,
  input  a3,
  input  a2,
  input  a1,
  output out_33,
  output out_34,
  output out_35,
  output out_36,
  output out_37,
  output out_38,
  output out_39,
  output out_40,
  output out_41,
  output out_42,
  output out_43,
  output out_44,
  output out_45,
  output out_46,
  output out_47,
  output out_48
);

  wire ic_74283_2_cout, ic_74283_3_cout, ic_74283_4_cout, not_1_out, not_2_out, not_3_out, not_4_out,
       not_5_out, not_6_out, not_7_out, not_8_out, not_9_out, not_10_out, not_11_out, not_12_out, not_13_out,
       not_14_out, not_15_out, not_16_out;

  not not_1 (not_1_out, b15);
  not not_2 (not_2_out, b16);
  not not_3 (not_3_out, b14);
  not not_4 (not_4_out, b13);
  IC_74283 ic_74283_1 (
    .CIN(ic_74283_2_cout), .A1(a13), .B1(not_4_out), .A2(a14), .B2(not_3_out), .A3(a15), .B3(not_1_out),
    .A4(a16), .B4(not_2_out), .Y1(out_36), .Y2(out_35), .Y3(out_34), .Y4(out_33));  // open: COUT
  not not_5 (not_5_out, b12);
  not not_6 (not_6_out, b11);
  not not_7 (not_7_out, b9);
  not not_8 (not_8_out, b10);
  IC_74283 ic_74283_2 (
    .CIN(ic_74283_3_cout), .A1(a9), .B1(not_7_out), .A2(a10), .B2(not_8_out), .A3(a11), .B3(not_6_out),
    .A4(a12), .B4(not_5_out), .Y1(out_40), .Y2(out_39), .Y3(out_38), .Y4(out_37), .COUT(ic_74283_2_cout));
  not not_9 (not_9_out, b6);
  not not_10 (not_10_out, b5);
  not not_11 (not_11_out, b7);
  not not_12 (not_12_out, b8);
  IC_74283 ic_74283_3 (
    .CIN(ic_74283_4_cout), .A1(a5), .B1(not_10_out), .A2(a6), .B2(not_9_out), .A3(a7), .B3(not_11_out),
    .A4(a8), .B4(not_12_out), .Y1(out_44), .Y2(out_43), .Y3(out_42), .Y4(out_41), .COUT(ic_74283_3_cout));
  not not_13 (not_13_out, b3);
  not not_14 (not_14_out, b1);
  not not_15 (not_15_out, b4);
  not not_16 (not_16_out, b2);
  IC_74283 ic_74283_4 (
    .CIN(1'b1), .A1(a1), .B1(not_14_out), .A2(a2), .B2(not_16_out), .A3(a3), .B3(not_13_out), .A4(a4),
    .B4(not_15_out), .Y1(out_48), .Y2(out_47), .Y3(out_46), .Y4(out_45), .COUT(ic_74283_4_cout));
endmodule

module RFID_Date_Set (
  input  MSB,
  input  in_2,
  input  in_3,
  input  in_4,
  input  in_5,
  input  in_6,
  input  in_7,
  input  in_8,
  input  in_9,
  input  in_10,
  input  in_11,
  input  in_12,
  input  in_13,
  input  in_14,
  input  in_15,
  input  LSB,
  input  set
);

  wire and_1_out, and_2_out, and_3_out, and_4_out, and_5_out, and_6_out, and_7_out, and_8_out, and_9_out,
       and_10_out, and_11_out, and_12_out, and_13_out, and_14_out, and_15_out, and_16_out;

  and and_1 (and_1_out, in_2, set);
  and and_2 (and_2_out, in_3, set);
  and and_3 (and_3_out, MSB, set);
  and and_4 (and_4_out, in_5, set);
  and and_5 (and_5_out, in_4, set);
  and and_6 (and_6_out, in_7, set);
  and and_7 (and_7_out, in_6, set);
  and and_8 (and_8_out, in_8, set);
  and and_9 (and_9_out, in_11, set);
  and and_10 (and_10_out, in_9, set);
  and and_11 (and_11_out, in_10, set);
  and and_12 (and_12_out, in_13, set);
  and and_13 (and_13_out, in_12, set);
  and and_14 (and_14_out, LSB, set);
  and and_15 (and_15_out, in_14, set);
  and and_16 (and_16_out, in_15, set);
endmodule

module UP_DOWN_COUNTER (
  input  up,
  input  down,
  output a0,
  output a1,
  output a2,
  output a3
);

  wire and_1_out, and_2_out, and_3_out, and_4_out, ic_74283_1_y1, ic_74283_1_y2, ic_74283_1_y3,
       ic_74283_1_y4, or_1_out, or_2_out;

  or or_1 (or_1_out, up, down);
  and and_1 (and_1_out, or_1_out, 1'b1);
  and and_2 (and_2_out, down, 1'b1);
  and and_3 (and_3_out, down, 1'b1);
  and and_4 (and_4_out, down, 1'b1);
  IC_74283 ic_74283_1 (
    .CIN(1'b0), .A1(and_1_out), .B1(a0), .A2(and_2_out), .B2(a1), .A3(and_3_out), .B3(a2), .A4(and_4_out),
    .B4(a3), .Y1(ic_74283_1_y1), .Y2(ic_74283_1_y2), .Y3(ic_74283_1_y3), .Y4(ic_74283_1_y4));  // open: COUT
  or or_2 (or_2_out, down, up);
  D_Flip_Flop #(.trigger("falling")) d_ff_1 (.clk(or_2_out), .D(ic_74283_1_y1), .Q(a0));  // open: Qn, preset, en, reset
  D_Flip_Flop #(.trigger("falling")) d_ff_2 (.clk(or_2_out), .D(ic_74283_1_y2), .Q(a1));  // open: Qn, preset, en, reset
  D_Flip_Flop #(.trigger("falling")) d_ff_3 (.clk(or_2_out), .D(ic_74283_1_y3), .Q(a2));  // open: Qn, preset, en, reset
  D_Flip_Flop #(.trigger("falling")) d_ff_4 (.clk(or_2_out), .D(ic_74283_1_y4), .Q(a3));  // open: Qn, preset, en, reset
endmodule
