// Logisim project compare.circ as structural Verilog: 1 circuit, main circuit main
module main (
  input  in_1,
  input  in_2,
  input  in_3,
  input  in_4,
  input  in_5,
  output out_6,
  output out_7,
  output out_8,
  output out_9,
  output [3:0] out_10,
  output [3:0] out_11
);

  wire clock_1_out, comparator_1_eq, comparator_1_gt, comparator_1_lt, j_k_ff_2_qn, j_k_ff_3_qn, j_k_ff_4_qn,
       n7_segment_display_driver_1_p5, n7_segment_display_driver_1_p6, n7_segment_display_driver_1_p7,
       n7_segment_display_driver_1_p8, n7_segment_display_driver_1_p9, n7_segment_display_driver_1_p10,
       n7_segment_display_driver_1_p11, n7_segment_display_driver_2_p5, n7_segment_display_driver_2_p6,
       n7_segment_display_driver_2_p7, n7_segment_display_driver_2_p8, n7_segment_display_driver_2_p9,
       n7_segment_display_driver_2_p10, n7_segment_display_driver_2_p11;

  Clock clock_1 (.out(clock_1_out));
  J_K_Flip_Flop j_k_ff_1 (.J(in_1), .clk(j_k_ff_2_qn), .K(in_1), .Q(out_6));  // open: Qn, preset, en, reset
  J_K_Flip_Flop j_k_ff_2 (
    .J(in_1), .clk(j_k_ff_3_qn), .K(in_1), .Q(out_7), .Qn(j_k_ff_2_qn));  // open: preset, en, reset
  J_K_Flip_Flop j_k_ff_3 (
    .J(in_1), .clk(j_k_ff_4_qn), .K(in_1), .Q(out_8), .Qn(j_k_ff_3_qn));  // open: preset, en, reset
  J_K_Flip_Flop j_k_ff_4 (
    .J(in_1), .clk(clock_1_out), .K(in_1), .Q(out_9), .Qn(j_k_ff_4_qn));  // open: preset, en, reset
  // _7_segment_display_driver 7_segment_display_driver_1: pin names not known; wires that end beside it: out_6, out_7, out_8, out_9, n7_segment_display_driver_1_p5, n7_segment_display_driver_1_p6, n7_segment_display_driver_1_p7, n7_segment_display_driver_1_p8, n7_segment_display_driver_1_p9, n7_segment_display_driver_1_p10, n7_segment_display_driver_1_p11
  // _7_segment_display_driver 7_segment_display_driver_2: pin names not known; wires that end beside it: in_2, in_3, in_4, in_5, n7_segment_display_driver_2_p5, n7_segment_display_driver_2_p6, n7_segment_display_driver_2_p7, n7_segment_display_driver_2_p8, n7_segment_display_driver_2_p9, n7_segment_display_driver_2_p10, n7_segment_display_driver_2_p11
  _7_Segment_Display u_7_segment_display_1 (
    .g(n7_segment_display_driver_1_p11), .f(n7_segment_display_driver_1_p10),
    .a(n7_segment_display_driver_1_p5), .b(n7_segment_display_driver_1_p6),
    .e(n7_segment_display_driver_1_p9), .d(n7_segment_display_driver_1_p8), .c(n7_segment_display_driver_1_p7));  // open: dp
  _7_Segment_Display u_7_segment_display_2 (
    .g(n7_segment_display_driver_2_p11), .f(n7_segment_display_driver_2_p10),
    .a(n7_segment_display_driver_2_p5), .b(n7_segment_display_driver_2_p6),
    .e(n7_segment_display_driver_2_p9), .d(n7_segment_display_driver_2_p8), .c(n7_segment_display_driver_2_p7));  // open: dp
  LED led_1 (.in(comparator_1_gt));
  Comparator #(.width(4)) comparator_1 (
    .a({out_6, out_7, out_8, out_9}), .b({in_2, in_3, in_4, in_5}), .gt(comparator_1_gt),
    .eq(comparator_1_eq), .lt(comparator_1_lt));
  LED led_2 (.in(comparator_1_lt));
  LED led_3 (.in(comparator_1_eq));

  assign out_10 = {out_6, out_7, out_8, out_9};
  assign out_11 = {in_2, in_3, in_4, in_5};
endmodule
